# Fritzing sketch WheelControl (saved by Fritzing 0.9.3b)
breadboards: 1

parts:
  Mod1 = Raspberry Pi Pico
  OLED_I2C1 = OLED 128x64 I2C Monochrome Display
  S1 = H-Bridge with L298N
  M1 = Stepper Motor - Bipolar
  J1 = Power Jack [package=power_jack_combo]
  S2 = Pushbutton [package="[SMD]"]

nets:
  GND: Mod1.pin_3, Mod1.pin_8, Mod1.pin_13, Mod1.pin_18, Mod1.pin_23, Mod1.pin_28, Mod1.pin_33, Mod1.pin_38, Mod1.pin_42, OLED_I2C1.GND, S1.GND, S2.Pin_3, S2.Pin_4
  N1: Mod1.pin_16, OLED_I2C1.SCK
  N2: Mod1.pin_17, OLED_I2C1.SDA
  N3: Mod1.pin_19, S1.IN2
  N4: Mod1.pin_20, S1.IN1
  N5: Mod1.pin_21, S1.IN3
  N6: Mod1.pin_22, S1.IN4
  N7: Mod1.pin_24, S2.Pin_1, S2.Pin_2
  N8: Mod1.pin_39, S1.5V
  N9: S1.12V, J1.PWR
  N10: S1.M1-01, M1.C
  N11: S1.M1-02, M1.A
  N12: S1.M2-01, M1.B
  N13: S1.M2-02, M1.D

custom parts:
  Raspberry Pi Pico: Raspberry Pi Pico. Based around the RP2040 microcontroller the Pico is a low cost microcontroller device bringing Raspberry Pi quality, cost, and easy of use to the microcontroller space. Jan 2021, Split part in to two versions: tht (this one) and SMD. This one will drill holes for a .1 in header in pcb to allow plugging in the module as well as providing pads to solder the module to the top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
  H-Bridge with L298N: h-bridge
