# Fritzing sketch shutter_meta_tester (saved by Fritzing 0.9.3b)
breadboards: 1

parts:
  Arduino = Arduino Nano (Rev3.0)
  R2 = Resistor [tolerance=±5% resistance=220 package=THT]
  LED1 = LED - 5mm [color="Red (633nm)" package="5 mm [THT]"]
  S1 = Momentary Switch [package=ksa_sealed_tac_switch]
  LCD1 = LCD1602-I2C

nets (from the breadboard view):
  GND: Arduino.GND, LED1.cathode, S1.4, LCD1.GND
  N1: Arduino.D3, R2.Pin_1
  N2: Arduino.D4, S1.1
  5V: Arduino.5V, LCD1.VCC
  N3: Arduino.A5, LCD1.SCL
  N4: Arduino.A4, LCD1.SDA
  N5: R2.Pin_0, LED1.anode

custom parts:
  LCD1602-I2C: A standard character display, usually with 2x16 characters. Comes in many colors with LCM1602 IIC attached.
